// Logisim project mems.circ as structural Verilog: 3 circuits, main circuit mem_dados
module mem_dados (
  input  memWrite,
  input  [31:0] EL,
  input  [31:0] WD,
  input  memRead,
  output [31:0] LD
);

  wire and_1_out, and_2_out, and_3_out, and_4_out, and_5_out, and_6_out, and_7_out, and_8_out, and_9_out,
       and_10_out, and_11_out, and_12_out, and_13_out, and_14_out, and_15_out, and_16_out, and_17_out,
       and_18_out, and_19_out, and_20_out, and_21_out, and_22_out, and_23_out, and_24_out, and_25_out,
       and_26_out, and_27_out, and_28_out, and_29_out, and_30_out, and_31_out, and_32_out, latch00_q,
       latch01_q, latch02_q, latch03_q, latch04_q, latch05_q, latch06_q, latch07_q, latch08_q, latch09_q,
       latch10_q, latch11_q, latch12_q, latch13_q, latch14_q, latch15_q, latch16_q, latch17_q, latch18_q,
       latch19_q, latch20_q, latch21_q, latch22_q, latch23_q, latch24_q, latch25_q, latch26_q, latch27_q,
       latch28_q, latch29_q, latch30_q, latch31_q, LOAD_STORY, or_1_out;

  or or_1 (or_1_out, memWrite, memRead);
  xor xor_1 (LOAD_STORY, or_1_out, memRead);
  and and_1 (and_1_out, EL[0], LOAD_STORY);
  and and_2 (and_2_out, EL[4], LOAD_STORY);
  and and_3 (and_3_out, EL[8], LOAD_STORY);
  and and_4 (and_4_out, EL[12], LOAD_STORY);
  and and_5 (and_5_out, EL[16], LOAD_STORY);
  and and_6 (and_6_out, EL[20], LOAD_STORY);
  and and_7 (and_7_out, EL[24], LOAD_STORY);
  and and_8 (and_8_out, EL[28], LOAD_STORY);
  latch_D latch00 (.E(and_1_out), .D(WD[0]), .Q(latch00_q));  // open: Q_2
  latch_D latch04 (.E(and_2_out), .D(WD[4]), .Q(latch04_q));  // open: Q_2
  latch_D latch08 (.E(and_3_out), .D(WD[8]), .Q(latch08_q));  // open: Q_2
  latch_D latch12 (.E(and_4_out), .D(WD[12]), .Q(latch12_q));  // open: Q_2
  latch_D latch16 (.E(and_5_out), .D(WD[16]), .Q(latch16_q));  // open: Q_2
  latch_D latch20 (.E(and_6_out), .D(WD[20]), .Q(latch20_q));  // open: Q_2
  latch_D latch24 (.E(and_7_out), .D(WD[24]), .Q(latch24_q));  // open: Q_2
  latch_D latch28 (.E(and_8_out), .D(WD[28]), .Q(latch28_q));  // open: Q_2
  assign LD[0] = EL[0] ? latch00_q : 1'bz;  // Controlled_Buffer controlled_buffer_1
  assign LD[4] = EL[4] ? latch04_q : 1'bz;  // Controlled_Buffer controlled_buffer_2
  assign LD[8] = EL[8] ? latch08_q : 1'bz;  // Controlled_Buffer controlled_buffer_3
  assign LD[12] = EL[12] ? latch12_q : 1'bz;  // Controlled_Buffer controlled_buffer_4
  assign LD[16] = EL[16] ? latch16_q : 1'bz;  // Controlled_Buffer controlled_buffer_5
  assign LD[20] = EL[20] ? latch20_q : 1'bz;  // Controlled_Buffer controlled_buffer_6
  assign LD[24] = EL[24] ? latch24_q : 1'bz;  // Controlled_Buffer controlled_buffer_7
  assign LD[28] = EL[28] ? latch28_q : 1'bz;  // Controlled_Buffer controlled_buffer_8
  and and_9 (and_9_out, EL[1], LOAD_STORY);
  and and_10 (and_10_out, EL[5], LOAD_STORY);
  and and_11 (and_11_out, EL[9], LOAD_STORY);
  and and_12 (and_12_out, EL[13], LOAD_STORY);
  and and_13 (and_13_out, EL[17], LOAD_STORY);
  and and_14 (and_14_out, EL[21], LOAD_STORY);
  and and_15 (and_15_out, EL[25], LOAD_STORY);
  and and_16 (and_16_out, EL[29], LOAD_STORY);
  assign LD[1] = EL[1] ? latch01_q : 1'bz;  // Controlled_Buffer controlled_buffer_9
  latch_D latch01 (.E(and_9_out), .D(WD[1]), .Q(latch01_q));  // open: Q_2
  assign LD[5] = EL[5] ? latch05_q : 1'bz;  // Controlled_Buffer controlled_buffer_10
  latch_D latch05 (.E(and_10_out), .D(WD[5]), .Q(latch05_q));  // open: Q_2
  assign LD[9] = EL[9] ? latch09_q : 1'bz;  // Controlled_Buffer controlled_buffer_11
  latch_D latch09 (.E(and_11_out), .D(WD[9]), .Q(latch09_q));  // open: Q_2
  latch_D latch13 (.E(and_12_out), .D(WD[13]), .Q(latch13_q));  // open: Q_2
  assign LD[13] = EL[13] ? latch13_q : 1'bz;  // Controlled_Buffer controlled_buffer_12
  latch_D latch17 (.E(and_13_out), .D(WD[17]), .Q(latch17_q));  // open: Q_2
  assign LD[17] = EL[17] ? latch17_q : 1'bz;  // Controlled_Buffer controlled_buffer_13
  latch_D latch21 (.E(and_14_out), .D(WD[21]), .Q(latch21_q));  // open: Q_2
  assign LD[21] = EL[21] ? latch21_q : 1'bz;  // Controlled_Buffer controlled_buffer_14
  assign LD[25] = EL[25] ? latch25_q : 1'bz;  // Controlled_Buffer controlled_buffer_15
  latch_D latch25 (.E(and_15_out), .D(WD[25]), .Q(latch25_q));  // open: Q_2
  latch_D latch29 (.E(and_16_out), .D(WD[29]), .Q(latch29_q));  // open: Q_2
  assign LD[29] = EL[29] ? latch29_q : 1'bz;  // Controlled_Buffer controlled_buffer_16
  and and_17 (and_17_out, EL[2], LOAD_STORY);
  latch_D latch02 (.E(and_17_out), .D(WD[2]), .Q(latch02_q));  // open: Q_2
  and and_18 (and_18_out, EL[6], LOAD_STORY);
  latch_D latch06 (.E(and_18_out), .D(WD[6]), .Q(latch06_q));  // open: Q_2
  and and_19 (and_19_out, EL[10], LOAD_STORY);
  latch_D latch10 (.E(and_19_out), .D(WD[10]), .Q(latch10_q));  // open: Q_2
  and and_20 (and_20_out, EL[14], LOAD_STORY);
  latch_D latch14 (.E(and_20_out), .D(WD[14]), .Q(latch14_q));  // open: Q_2
  and and_21 (and_21_out, EL[18], LOAD_STORY);
  latch_D latch18 (.E(and_21_out), .D(WD[18]), .Q(latch18_q));  // open: Q_2
  and and_22 (and_22_out, EL[22], LOAD_STORY);
  latch_D latch22 (.E(and_22_out), .D(WD[22]), .Q(latch22_q));  // open: Q_2
  and and_23 (and_23_out, EL[26], LOAD_STORY);
  latch_D latch26 (.E(and_23_out), .D(WD[26]), .Q(latch26_q));  // open: Q_2
  and and_24 (and_24_out, EL[30], LOAD_STORY);
  latch_D latch30 (.E(and_24_out), .D(WD[30]), .Q(latch30_q));  // open: Q_2
  assign LD[2] = EL[2] ? latch02_q : 1'bz;  // Controlled_Buffer controlled_buffer_17
  assign LD[6] = EL[6] ? latch06_q : 1'bz;  // Controlled_Buffer controlled_buffer_18
  assign LD[10] = EL[10] ? latch10_q : 1'bz;  // Controlled_Buffer controlled_buffer_19
  assign LD[14] = EL[14] ? latch14_q : 1'bz;  // Controlled_Buffer controlled_buffer_20
  assign LD[18] = EL[18] ? latch18_q : 1'bz;  // Controlled_Buffer controlled_buffer_21
  assign LD[22] = EL[22] ? latch22_q : 1'bz;  // Controlled_Buffer controlled_buffer_22
  assign LD[26] = EL[26] ? latch26_q : 1'bz;  // Controlled_Buffer controlled_buffer_23
  assign LD[30] = EL[30] ? latch30_q : 1'bz;  // Controlled_Buffer controlled_buffer_24
  and and_25 (and_25_out, EL[3], LOAD_STORY);
  latch_D latch03 (.E(and_25_out), .D(WD[3]), .Q(latch03_q));  // open: Q_2
  and and_26 (and_26_out, EL[7], LOAD_STORY);
  latch_D latch07 (.E(and_26_out), .D(WD[7]), .Q(latch07_q));  // open: Q_2
  and and_27 (and_27_out, EL[11], LOAD_STORY);
  latch_D latch11 (.E(and_27_out), .D(WD[11]), .Q(latch11_q));  // open: Q_2
  and and_28 (and_28_out, EL[15], LOAD_STORY);
  latch_D latch15 (.E(and_28_out), .D(WD[15]), .Q(latch15_q));  // open: Q_2
  and and_29 (and_29_out, EL[19], LOAD_STORY);
  latch_D latch19 (.E(and_29_out), .D(WD[19]), .Q(latch19_q));  // open: Q_2
  and and_30 (and_30_out, EL[23], LOAD_STORY);
  latch_D latch23 (.E(and_30_out), .D(WD[23]), .Q(latch23_q));  // open: Q_2
  and and_31 (and_31_out, EL[27], LOAD_STORY);
  latch_D latch27 (.E(and_31_out), .D(WD[27]), .Q(latch27_q));  // open: Q_2
  and and_32 (and_32_out, EL[31], LOAD_STORY);
  latch_D latch31 (.E(and_32_out), .D(WD[31]), .Q(latch31_q));  // open: Q_2
  assign LD[3] = EL[3] ? latch03_q : 1'bz;  // Controlled_Buffer controlled_buffer_25
  assign LD[7] = EL[7] ? latch07_q : 1'bz;  // Controlled_Buffer controlled_buffer_26
  assign LD[11] = EL[11] ? latch11_q : 1'bz;  // Controlled_Buffer controlled_buffer_27
  assign LD[15] = EL[15] ? latch15_q : 1'bz;  // Controlled_Buffer controlled_buffer_28
  assign LD[19] = EL[19] ? latch19_q : 1'bz;  // Controlled_Buffer controlled_buffer_29
  assign LD[23] = EL[23] ? latch23_q : 1'bz;  // Controlled_Buffer controlled_buffer_30
  assign LD[27] = EL[27] ? latch27_q : 1'bz;  // Controlled_Buffer controlled_buffer_31
  assign LD[31] = EL[31] ? latch31_q : 1'bz;  // Controlled_Buffer controlled_buffer_32

  // Other names for the same wires on the sheet: E00 = EL[0]; E01 = EL[1]; E02 = EL[2]; E03 = EL[3]; E04 = EL[4];
  //   E05 = EL[5]; E06 = EL[6]; E07 = EL[7]; E08 = EL[8]; E09 = EL[9]; E10 = EL[10]; E11 = EL[11]; E12 = EL[12];
  //   E13 = EL[13]; E14 = EL[14]; E15 = EL[15]; E16 = EL[16]; E17 = EL[17]; E18 = EL[18]; E19 = EL[19]; E20 = EL[20];
  //   E21 = EL[21]; E22 = EL[22]; E23 = EL[23]; E24 = EL[24]; E25 = EL[25]; E26 = EL[26]; E27 = EL[27]; E28 = EL[28];
  //   E29 = EL[29]; E30 = EL[30]; E31 = EL[31]; D00 = WD[0]; D01 = WD[1]; D02 = WD[2]; D03 = WD[3]; D04 = WD[4];
  //   D05 = WD[5]; D06 = WD[6]; D07 = WD[7]; D08 = WD[8]; D09 = WD[9]; D10 = WD[10]; D11 = WD[11]; D12 = WD[12];
  //   D13 = WD[13]; D14 = WD[14]; D15 = WD[15]; D16 = WD[16]; D17 = WD[17]; D18 = WD[18]; D19 = WD[19]; D20 = WD[20];
  //   D21 = WD[21]; D22 = WD[22]; D23 = WD[23]; D24 = WD[24]; D25 = WD[25]; D26 = WD[26]; D27 = WD[27]; D28 = WD[28];
  //   D29 = WD[29]; D30 = WD[30]; D31 = WD[31]
endmodule

module mem_instrucoes (
  input  CLK,
  input  reset,
  input  [31:0] endereco_instr,
  output [31:0] instrucao
);

  wire [31:0] ram_1_data;

  RAM #(.addrWidth(24), .dataWidth(32)) ram_1 (
    .addr(endereco_instr[25:2]), .data(ram_1_data), .ld(1'b1));  // open: sel, clk, clr
  Register #(.width(32)) micro_instru (.D(ram_1_data), .Q(instrucao), .clk(CLK), .clr(reset));  // open: en
endmodule

// Latch
module latch_D (
  input  E,
  input  D,
  output Q,
  output Q_2
);

  wire and_1_out, and_2_out, not_1_out;

  not not_1 (not_1_out, D);
  and and_1 (and_1_out, not_1_out, E);
  and and_2 (and_2_out, E, D);
  nor nor_1 (Q, and_1_out, Q_2);
  nor nor_2 (Q_2, Q, and_2_out);
endmodule
